# Fritzing sketch Baby_R2_Board (saved by Fritzing 0.9.6b)
circuit board: 8.46667cm x 5.64444cm
breadboards: 1

parts:
  U1 = NodeMCU V1.0
  Right_Leg = Basic Servo
  Head = Basic Servo
  Left_Leg = Basic Servo
  Q1 = TIP120 Hi-Current Darlington Transistor
  SP1 = SPEAKER [package=pcb_mount_speaker]
  S1 = Toggle Switch [package=THT]

nets:
  N1: U1.D5, Left_Leg.pulse
  N2: U1.D6, Right_Leg.pulse
  N3: U1.D7, Head.pulse
  N4: U1.RX, S1.COM
  GND: Right_Leg.gnd, Head.gnd, Left_Leg.gnd, SP1.+
  VCC: Right_Leg.vcc, Head.vcc, Left_Leg.vcc, Q1.EMITTER
  N5: Q1.BASE, S1.L2
  N6: Q1.COLLECTOR, SP1.-

custom parts:
  NodeMCU V1.0: ESP8266 based NodeMCU
